// Logisim project Sanganak.circ as structural Verilog: 15 circuits, main circuit CU
module main (
  input  [15:0] in_1,
  input  [2:0] in_2
);

  wire button_2_out, button_3_out, clock_1_out;
  wire [7:0] bc1_1_outr_out;
  wire [15:0] bc1_1_bus_out;

  Button button_1 ();  // open: out
  BC1 bc1_1 (
    .we_ram(button_2_out), .INPR_INP(8'hab), .LD_OUTR(button_3_out), .CLK(clock_1_out), .MAN_INP(in_1),
    .S2(in_2[2]), .S1(in_2[1]), .S0(in_2[0]), .OUTR_OUT(bc1_1_outr_out), .BUS_OUT(bc1_1_bus_out));  // open: ALU_CTRL, CLR_AR, INR_AR, LD_PC, CLR_PC, INR_PC, LD_DR, CLR_DR, INR_DR, LD_AC, CLR_AC, INR_AC, LD_TR, CLR_TR, INR_TR, LD_IR, LD_AR, E_OUT, IR_Q
  Button button_2 (.out(button_2_out));
  Clock clock_1 (.out(clock_1_out));
  Button button_3 (.out(button_3_out));
  // Probe on bc1_1_bus_out
  // Probe on bc1_1_outr_out
endmodule

module AR (
  input  [11:0] DATA,
  input  LD,
  input  CLK,
  input  CLR,
  input  INR,
  output [11:0] out_6
);

  wire or_1_out;
  wire [11:0] adder_1_out, multiplexer_1_out;

  or or_1 (or_1_out, LD, INR);
  Register #(.width(12)) register_1 (.D(multiplexer_1_out), .en(or_1_out), .clk(CLK), .Q(out_6), .clr(CLR));
  Multiplexer #(.width(12)) multiplexer_1 (.in0(DATA), .in1(adder_1_out), .out(multiplexer_1_out), .sel(INR));
  Adder #(.width(12)) adder_1 (.a(out_6), .b(12'h1), .out(adder_1_out));  // open: cin, cout
endmodule

module PC (
  input  [11:0] DATA,
  input  LD,
  input  CLK,
  input  CLR,
  input  INR,
  output [11:0] out_6
);

  wire or_1_out;
  wire [11:0] adder_1_out, multiplexer_1_out;

  or or_1 (or_1_out, LD, INR);
  Register #(.width(12)) register_1 (.D(multiplexer_1_out), .en(or_1_out), .clk(CLK), .Q(out_6), .clr(CLR));
  Multiplexer #(.width(12)) multiplexer_1 (.in0(DATA), .in1(adder_1_out), .out(multiplexer_1_out), .sel(INR));
  Adder #(.width(12)) adder_1 (.a(out_6), .b(12'h1), .out(adder_1_out));  // open: cin, cout
endmodule

module DR (
  input  [15:0] DATA,
  input  LD,
  input  CLK,
  input  CLR,
  input  INR,
  output [15:0] out_6
);

  wire or_1_out;
  wire [15:0] adder_1_out, multiplexer_1_out;

  or or_1 (or_1_out, LD, INR);
  Register #(.width(16)) register_1 (.D(multiplexer_1_out), .en(or_1_out), .clk(CLK), .Q(out_6), .clr(CLR));
  Multiplexer #(.width(16)) multiplexer_1 (.in0(DATA), .in1(adder_1_out), .out(multiplexer_1_out), .sel(INR));
  Adder #(.width(16)) adder_1 (.a(out_6), .b(16'h1), .out(adder_1_out));  // open: cin, cout
endmodule

module AC (
  input  [15:0] DATA,
  input  LD,
  input  CLK,
  input  CLR,
  input  INR,
  output [15:0] out_6
);

  wire or_1_out;
  wire [15:0] adder_1_out, multiplexer_1_out;

  or or_1 (or_1_out, LD, INR);
  Register #(.width(16)) register_1 (.D(multiplexer_1_out), .en(or_1_out), .clk(CLK), .Q(out_6), .clr(CLR));
  Multiplexer #(.width(16)) multiplexer_1 (.in0(DATA), .in1(adder_1_out), .out(multiplexer_1_out), .sel(INR));
  Adder #(.width(16)) adder_1 (.a(out_6), .b(16'h1), .out(adder_1_out));  // open: cin, cout
endmodule

module TR (
  input  [15:0] DATA,
  input  LD,
  input  CLK,
  input  CLR,
  input  INR,
  output [15:0] out_6
);

  wire or_1_out;
  wire [15:0] adder_1_out, multiplexer_1_out;

  or or_1 (or_1_out, LD, INR);
  Register #(.width(16)) register_1 (.D(multiplexer_1_out), .en(or_1_out), .clk(CLK), .Q(out_6), .clr(CLR));
  Multiplexer #(.width(16)) multiplexer_1 (.in0(DATA), .in1(adder_1_out), .out(multiplexer_1_out), .sel(INR));
  Adder #(.width(16)) adder_1 (.a(out_6), .b(16'h1), .out(adder_1_out));  // open: cin, cout
endmodule

module IR (
  input  [15:0] DATA,
  input  LD,
  input  CLOCK,
  output [15:0] out_4
);

  Register #(.width(16)) register_1 (.D(DATA), .en(LD), .clk(CLOCK), .Q(out_4));  // open: clr
endmodule

module INPR (
  input  [7:0] DATA,
  input  LD,
  input  CLOCK,
  output [7:0] out_4
);

  Register register_1 (.D(DATA), .en(LD), .clk(CLOCK), .Q(out_4));  // open: clr
endmodule

module OUTR (
  input  [7:0] DATA,
  input  LD,
  input  CLOCK,
  output [7:0] out_4
);

  Register register_1 (.D(DATA), .en(LD), .clk(CLOCK), .Q(out_4));  // open: clr
endmodule

module check (
  input  [11:0] in_1
);

  wire button_1_out, button_2_out, button_3_out, clock_1_out;
  wire [11:0] ar_1_out_6;

  Button button_1 (.out(button_1_out));
  Clock clock_1 (.out(clock_1_out));
  Button button_2 (.out(button_2_out));
  Button button_3 (.out(button_3_out));
  // Probe on ar_1_out_6
  AR ar_1 (
    .DATA(in_1), .LD(button_1_out), .CLK(clock_1_out), .CLR(button_2_out), .INR(button_3_out),
    .out_6(ar_1_out_6));
endmodule

module main_test (
  input  we_ram,
  input  in_2,
  input  in_3,
  input  in_4
);

  wire button_1_out, button_2_out, button_3_out, button_4_out, button_5_out, button_6_out, button_7_out,
       button_8_out, button_9_out, button_10_out, button_11_out, button_12_out, button_13_out, button_14_out,
       button_15_out, button_16_out, button_17_out, button_18_out, CLK;
  wire [3:0] multiplexer_1_out_2;
  wire [7:0] inpr_1_out_4, outr_1_out_4;
  wire [11:0] ar_1_out_6, multiplexer_1_out, pc_1_out_6;
  wire [15:0] ac_1_out_6, dr_1_out_6, ir_1_out_4, tr_1_out_6;

  Button button_1 (.out(button_1_out));
  Button button_2 (.out(button_2_out));
  Button button_3 (.out(button_3_out));
  Button button_4 (.out(button_4_out));
  Button button_5 (.out(button_5_out));
  Button button_6 (.out(button_6_out));
  Button button_7 (.out(button_7_out));
  Button button_8 (.out(button_8_out));
  Button button_9 (.out(button_9_out));
  Button button_10 (.out(button_10_out));
  Button button_11 (.out(button_11_out));
  Button button_12 (.out(button_12_out));
  Button button_13 (.out(button_13_out));
  Button button_14 (.out(button_14_out));
  Button button_15 (.out(button_15_out));
  Button button_16 (.out(button_16_out));
  Button button_17 (.out(button_17_out));
  Button button_18 (.out(button_18_out));
  Clock clock_1 (.out(CLK));
  AR ar_1 (
    .DATA(multiplexer_1_out), .LD(button_1_out), .CLK(CLK), .CLR(button_2_out), .INR(button_3_out),
    .out_6(ar_1_out_6));
  PC pc_1 (
    .DATA(multiplexer_1_out), .LD(button_4_out), .CLK(CLK), .CLR(button_5_out), .INR(button_6_out),
    .out_6(pc_1_out_6));
  DR dr_1 (
    .DATA({multiplexer_1_out_2, multiplexer_1_out}), .LD(button_7_out), .CLK(CLK), .CLR(button_8_out),
    .INR(button_9_out), .out_6(dr_1_out_6));
  AC ac_1 (
    .DATA({multiplexer_1_out_2, multiplexer_1_out}), .LD(button_10_out), .CLK(CLK), .CLR(button_11_out),
    .INR(button_12_out), .out_6(ac_1_out_6));
  TR tr_1 (
    .DATA({multiplexer_1_out_2, multiplexer_1_out}), .LD(button_13_out), .CLK(CLK), .CLR(button_14_out),
    .INR(button_15_out), .out_6(tr_1_out_6));
  IR ir_1 (.DATA({multiplexer_1_out_2, multiplexer_1_out}), .LD(button_16_out), .CLOCK(CLK), .out_4(ir_1_out_4));
  INPR inpr_1 (.LD(button_17_out), .CLOCK(CLK), .out_4(inpr_1_out_4));  // open: DATA
  OUTR outr_1 (.LD(button_18_out), .CLOCK(CLK), .out_4(outr_1_out_4));  // open: DATA
  Multiplexer #(.select(3), .width(16)) multiplexer_1 (
    .in0({4'b0000, pc_1_out_6}), .in1(dr_1_out_6), .in2(ac_1_out_6), .in3(tr_1_out_6), .in4(ir_1_out_4),
    .in5({{8{1'b0}}, inpr_1_out_4}), .in6({{8{1'b0}}, outr_1_out_4}), .in7({16{1'b0}}),
    .out({multiplexer_1_out_2, multiplexer_1_out}), .sel({in_2, in_3, in_4}));
  // Probe on {multiplexer_1_out_2, multiplexer_1_out}
  RAM #(.addrWidth(12), .dataWidth(16)) ram_1 (.addr(ar_1_out_6), .we(we_ram), .clk(CLK));  // open: oe, din, dout
endmodule

module BC1 (
  input  CLK,
  input  we_ram,
  input  LD_AR,
  input  CLR_AR,
  input  INR_AR,
  input  LD_PC,
  input  CLR_PC,
  input  INR_PC,
  input  LD_DR,
  input  [15:0] MAN_INP,
  input  CLR_DR,
  input  INR_DR,
  input  S2,
  input  S1,
  input  S0,
  input  LD_AC,
  input  CLR_AC,
  input  [2:0] ALU_CTRL,
  input  INR_AC,
  input  LD_TR,
  input  CLR_TR,
  input  INR_TR,
  input  LD_IR,
  input  [7:0] INPR_INP,
  input  LD_OUTR,
  output [15:0] BUS_OUT,
  output E_OUT,
  output [15:0] IR_Q,
  output [7:0] OUTR_OUT
);

  wire [7:0] inpr_1_out_4;
  wire [11:0] ar_1_out_6, pc_1_out_6;
  wire [15:0] ac_1_out_6, alu_1_alu_out, dr_1_out_6, ram_1_dout, tr_1_out_6;

  ALU alu_1 (
    .INPR(inpr_1_out_4), .AC(ac_1_out_6), .DR(dr_1_out_6), .OP_SEL(ALU_CTRL), .E_OUT(E_OUT),
    .ALU_OUT(alu_1_alu_out));
  AR ar_1 (.DATA(BUS_OUT[11:0]), .LD(LD_AR), .CLK(CLK), .CLR(CLR_AR), .INR(INR_AR), .out_6(ar_1_out_6));
  // Probe on pc_1_out_6
  PC pc_1 (.DATA(BUS_OUT[11:0]), .LD(LD_PC), .CLK(CLK), .CLR(CLR_PC), .INR(INR_PC), .out_6(pc_1_out_6));
  DR dr_1 (.DATA(BUS_OUT), .LD(LD_DR), .CLK(CLK), .CLR(CLR_DR), .INR(INR_DR), .out_6(dr_1_out_6));
  AC ac_1 (.DATA(alu_1_alu_out), .LD(LD_AC), .CLK(CLK), .CLR(CLR_AC), .INR(INR_AC), .out_6(ac_1_out_6));
  TR tr_1 (.DATA(BUS_OUT), .LD(LD_TR), .CLK(CLK), .CLR(CLR_TR), .INR(INR_TR), .out_6(tr_1_out_6));
  IR ir_1 (.DATA(BUS_OUT), .LD(LD_IR), .CLOCK(CLK), .out_4(IR_Q));
  INPR inpr_1 (.DATA(INPR_INP), .LD(1'b1), .CLOCK(CLK), .out_4(inpr_1_out_4));
  OUTR outr_1 (.DATA(BUS_OUT[7:0]), .LD(LD_OUTR), .CLOCK(CLK), .out_4(OUTR_OUT));
  // Probe on ar_1_out_6
  // Probe on dr_1_out_6
  // Probe on ac_1_out_6
  Multiplexer #(.select(3), .width(16)) multiplexer_1 (
    .in0({4'b0000, pc_1_out_6}), .in1(dr_1_out_6), .in2(ac_1_out_6), .in3(tr_1_out_6), .in4(IR_Q),
    .in5({4'b0000, ar_1_out_6}), .in6(MAN_INP), .in7(ram_1_dout), .out(BUS_OUT), .sel({S2, S1, S0}));
  // Probe on BUS_OUT
  // Probe on ram_1_dout
  RAM #(.addrWidth(12), .asyncread("true"), .dataWidth(16), .\type ("nonvolatile")) ram_1 (
    .addr(ar_1_out_6), .we(we_ram), .clk(CLK), .din(BUS_OUT), .dout(ram_1_dout));  // open: oe
endmodule

module ALU (
  input  [15:0] AC,
  input  [15:0] DR,
  input  [7:0] INPR,
  input  [2:0] OP_SEL,
  output E_OUT,
  output [15:0] ALU_OUT
);

  wire adder_1_cout;
  wire [15:0] adder_1_out, AND_OP_out, not_1_out;

  Adder #(.width(16)) adder_1 (.a(AC), .b(DR), .out(adder_1_out), .cout(adder_1_cout));  // open: cin
  assign not_1_out = ~AC;  // NOT_Gate not_1, 16 bits wide
  assign AND_OP_out = AC & DR;  // AND_Gate AND_OP, 16 bits wide
  buf or_1 (E_OUT, adder_1_cout);  // OR_Gate
  Multiplexer #(.select(3), .width(16)) multiplexer_1 (
    .in0(AND_OP_out), .in1(adder_1_out), .in2(not_1_out), .in3(DR), .in4({{8{1'b0}}, INPR}), .out(ALU_OUT),
    .sel(OP_SEL));  // open: in5, in6, in7
endmodule

module Power_button (
  input  BTN,
  input  CLK,
  output POWER_OUT
);

  T_Flip_Flop t_ff_1 (.T(BTN), .clk(CLK), .Q(POWER_OUT));  // open: Qn, reset, preset
endmodule

module CU (
  input  [15:0] IR_Q_MANUAL,
  input  CLR_T
);

  wire AC_out, and_20_out, AR_out, CLK, D0, D0_T4, D0_T5, D0_T6, D1, D1_T5, D2, D2_T4, D2_T5, D2_T6, D3,
       D3_T4, D3_T5, D4, D4_T4, D4_T5, D5, D5_T4, D5_T5, D5_T6, D6, D6_T4, D6_T5, D6_T6, D6_T7, D7, D7N_I_T3,
       DR_out, I, IR_out, nand_1_out, or_1_out, or_2_out, or_3_out, or_4_out, or_8_out, or_9_out, or_10_out,
       or_11_out, or_12_out, or_13_out, or_14_out, RAM_out, T0, T1, T2, T3, T4, T5, T6, T7, T8, T9, TR_out;
  wire [2:0] ALU_CTRL, MAIN_BUS;
  wire [3:0] Timing_counter_q;
  wire [11:0] ADDR;
  wire [14:12] IR_Q;
  wire [15:0] BUS_OUT;

  and and_1 (D4_T4, T4, D4);
  and and_2 (D2_T4, T4, D2);
  and and_3 (D3_T4, T4, D3);
  and and_4 (D5_T4, T4, D5);
  and and_5 (D6_T4, T4, D6);
  or or_1 (or_1_out, D0, D1);
  or or_2 (or_2_out, D0, D1);
  Clock clock_1 (.out(CLK));
  or or_3 (or_3_out, CLR_T, D0_T6, D2_T6, D3_T5, D4_T5, D5_T6, D6_T7);
  and and_6 (D3_T5, T5, D3);
  and and_7 (D2_T5, T5, D2);
  and and_8 (D7N_I_T3, T3, I, ~D7);  // AND_Gate
  and and_9 (D0_T4, T4, or_1_out);
  and and_10 (D0_T6, T6, or_2_out);
  and and_11 (D5_T5, T5, D5);
  or or_4 (or_4_out, T5, T6);
  and and_12 (D6_T5, or_4_out, D6);
  Counter #(.max('hf), .width(4)) Timing_counter (
    .clr(or_3_out), .clk(CLK), .Q(Timing_counter_q));  // open: load, up, count, D, carry
  and and_13 (D4_T5, T5, D4);
  and and_14 (D2_T6, T6, D2);
  and and_15 (D0_T5, T5, D0);
  and and_16 (D1_T5, T5, D1);
  and and_17 (D5_T6, T6, D5);
  and and_18 (D6_T6, T6, D6);
  Decoder #(.enable("false"), .select(3)) decoder_1 (
    .out0(D0), .out1(D1), .out2(D2), .out3(D3), .out4(D4), .out5(D5), .out6(D6), .out7(D7), .sel(IR_Q));
  Decoder #(.enable("false"), .select(4)) decoder_2 (
    .out0(T0), .out1(T1), .out2(T2), .out3(T3), .out4(T4), .out5(T5), .out6(T6), .out7(T7), .out8(T8),
    .out9(T9), .sel(Timing_counter_q));  // open: out10, out11, out12, out13, out14, out15
  and and_19 (D6_T7, T7, D6);
  or AR (AR_out, D4_T4, D5_T5);
  or DR (DR_out, D6_T5, D2_T5);
  or AC (AC_out, 1'b0, D3_T4);
  buf TR (TR_out, 1'b0);  // OR_Gate
  buf IR (IR_out, T2);  // OR_Gate
  or RAM (RAM_out, D2_T4, T1, D7N_I_T3, D0_T4, D6_T4);
  or or_5 (MAIN_BUS[2], IR_out, AR_out, RAM_out);
  or or_6 (MAIN_BUS[1], TR_out, RAM_out, AC_out);
  or or_7 (MAIN_BUS[0], RAM_out, TR_out, DR_out, AR_out);
  buf or_8 (or_8_out, D5_T4);  // OR_Gate
  or or_9 (or_9_out, T0, T2, D7N_I_T3);
  or or_10 (or_10_out, D4_T4, D5_T5);
  or or_11 (or_11_out, T1, D0_T4, D6_T4, D6_T5);
  or or_12 (or_12_out, D0_T5, D1_T5, D2_T5);
  and and_20 (and_20_out, D6_T6, nand_1_out);
  nand nand_1 (nand_1_out, BUS_OUT[0], BUS_OUT[1], BUS_OUT[2], BUS_OUT[3], BUS_OUT[4], BUS_OUT[5], BUS_OUT[6], BUS_OUT[7], BUS_OUT[9], BUS_OUT[10], BUS_OUT[11], BUS_OUT[12], BUS_OUT[13], BUS_OUT[14], BUS_OUT[15], BUS_OUT[8]);
  BC1 bc1_1 (
    .we_ram(or_14_out), .ALU_CTRL(ALU_CTRL), .INR_AR(or_8_out), .LD_PC(or_10_out), .INR_PC(or_13_out),
    .LD_DR(or_11_out), .INR_DR(D6_T5), .LD_AC(or_12_out), .LD_IR(T1), .LD_AR(or_9_out), .CLK(CLK),
    .S2(MAIN_BUS[2]), .S1(MAIN_BUS[1]), .S0(MAIN_BUS[0]), .IR_Q({I, IR_Q, ADDR}), .BUS_OUT(BUS_OUT));  // open: INPR_INP, CLR_AR, CLR_PC, CLR_DR, CLR_AC, INR_AC, LD_TR, CLR_TR, INR_TR, LD_OUTR, MAN_INP, E_OUT, OUTR_OUT
  or or_13 (or_13_out, and_20_out, T1);
  or or_14 (or_14_out, D3_T4, D6_T6, D5_T4);
  // Probe on {I, IR_Q, ADDR}
  buf or_15 (ALU_CTRL[2], 1'b0);  // OR_Gate
  or or_16 (ALU_CTRL[1], 1'b0, D2_T5);
  or or_17 (ALU_CTRL[0], 1'b0, D2_T5, D1_T5);

  // Other names for the same wires on the sheet: IR_Q (some bits) = {I, ADDR}

  // Notes on the sheet:
  //   D0 (000): AND
  //   D1 (001): ADD
  //   D2 (010): LDA
  //   D3 (011): STA
  //   D4 (100): BUN
  //   D5 (101): BSA
  //   D6 (110): ISZ
  //   D7 (111): Register-reference or I/O instructions
  //   D0
  //   T0
  //   T15
  //   D7
endmodule
